// Logisim project myCPU.circ as structural Verilog: 18 circuits, main circuit main
module main (
);

  wire alu_1_branch, alu_1_c, ctrl_1_out_3, ctrl_1_out_4, ctrl_1_out_6, ctrl_1_out_7, ctrl_1_out_8,
       ctrl_1_out_9, ctrl_1_out_10, dram_1_out_4, irom_1_out_2, multiplexer_1_out, multiplexer_2_out,
       multiplexer_3_out, multiplexer_4_out, npc_1_out_5, npc_1_out_6, pc_1_out_2, rf_1_out_6, rf_1_out_7,
       sext2_1_out_2, sext_1_out_3;
  wire [1:0] ctrl_1_out_5;

  NPC npc_1 (
    .in_1(pc_1_out_2), .in_2(sext_1_out_3), .in_3(rf_1_out_6), .in_4(ctrl_1_out_4), .out_5(npc_1_out_5),
    .out_6(npc_1_out_6));
  PC pc_1 (.in_1(npc_1_out_5), .out_2(pc_1_out_2));
  IROM irom_1 (.in_1(pc_1_out_2), .out_2(irom_1_out_2));
  CTRL ctrl_1 (
    .in_1(alu_1_c), .out_3(ctrl_1_out_3), .out_4(ctrl_1_out_4), .out_5(ctrl_1_out_5[0]),
    .out_6(ctrl_1_out_6), .out_7(ctrl_1_out_7), .out_8(ctrl_1_out_8), .out_9(ctrl_1_out_9),
    .out_10(ctrl_1_out_10), .in_2(irom_1_out_2));
  Multiplexer #(.select(2), .enable("false")) multiplexer_1 (
    .in0(npc_1_out_6), .in1(multiplexer_4_out), .in2(sext_1_out_3), .in3(dram_1_out_4),
    .out(multiplexer_1_out), .sel(ctrl_1_out_5));
  RF rf_1 (
    .in_1(irom_1_out_2), .in_2(irom_1_out_2), .in_3(multiplexer_1_out), .in_4(irom_1_out_2),
    .in_5(ctrl_1_out_3), .out_6(rf_1_out_6), .out_7(rf_1_out_7));
  SEXT sext_1 (.in_1(irom_1_out_2), .in_2(ctrl_1_out_6), .out_3(sext_1_out_3));
  Multiplexer #(.enable("false")) multiplexer_2 (
    .in0(pc_1_out_2), .in1(rf_1_out_6), .out(multiplexer_2_out), .sel(ctrl_1_out_8));
  Multiplexer #(.enable("false")) multiplexer_3 (
    .in0(rf_1_out_7), .in1(sext_1_out_3), .out(multiplexer_3_out), .sel(ctrl_1_out_9));
  Multiplexer #(.disabled(0), .enable("false")) multiplexer_4 (
    .in0(alu_1_branch), .in1(sext2_1_out_2), .out(multiplexer_4_out), .sel(ctrl_1_out_7));
  ALU alu_1 (.B(multiplexer_2_out), .alu_op(ctrl_1_out_7), .branch(alu_1_branch), .A(multiplexer_3_out), .C(alu_1_c));
  DRAM dram_1 (.in_1(alu_1_branch), .in_3(ctrl_1_out_10), .out_4(dram_1_out_4), .in_2(rf_1_out_7));
  SEXT2 sext2_1 (.in_1(dram_1_out_4), .out_2(sext2_1_out_2));
  // Pins of 1 and 2 bits meet at ctrl_1_out_5
endmodule

module PC (
  input  in_1,
  output out_2
);


  assign out_2 = in_1;
endmodule

module NPC (
  input  in_1,
  input  in_2,
  input  in_3,
  input  in_4,
  output out_5,
  output out_6
);
endmodule

module IROM (
  input  in_1,
  output out_2
);
endmodule

module CTRL (
  input  in_1,
  input  in_2,
  output out_3,
  output out_4,
  output out_5,
  output out_6,
  output out_7,
  output out_8,
  output out_9,
  output out_10
);
endmodule

module DRAM (
  input  in_1,
  input  in_2,
  input  in_3,
  output out_4
);
endmodule

module ALU (
  input  A,
  input  B,
  input  alu_op,
  output branch,
  output C
);

  wire not_1_out, not_2_out, \判断器2_1_out_2 , \判断器_1_out_2 , \加法器_1_out_4 , \桶形移位器_1_out_4 , \译码器_1_out_2 ,
       \选择器_1_out_4 , \选择器_2_out_4 , \逻辑运算_1_out_4 ;

  not not_1 (not_1_out, A);
  not not_2 (not_2_out, B);
  \桶形移位器  \u_桶形移位器_1  (.in_1(A), .in_2(B), .in_3(\译码器_1_out_2 ), .out_4(\桶形移位器_1_out_4 ));
  \逻辑运算  \u_逻辑运算_1  (.in_1(A), .in_2(B), .in_3(\译码器_1_out_2 ), .out_4(\逻辑运算_1_out_4 ));
  \译码器  \u_译码器_1  (.in_1(alu_op), .out_2(\译码器_1_out_2 ));
  \选择器  \u_选择器_1  (.in_1(A), .in_2(not_1_out), .in_3(\译码器_1_out_2 ), .out_4(\选择器_1_out_4 ));
  \选择器  \u_选择器_2  (.in_1(B), .in_2(not_2_out), .in_3(\译码器_1_out_2 ), .out_4(\选择器_2_out_4 ));
  \加法器  \u_加法器_1  (.in_1(\选择器_1_out_4 ), .in_2(\选择器_2_out_4 ), .in_3(\译码器_1_out_2 ), .out_4(\加法器_1_out_4 ));
  \判断器  \u_判断器_1  (.in_1(\加法器_1_out_4 ), .out_2(\判断器_1_out_2 ));
  \判断器2  \u_判断器2_1  (.in_1(\加法器_1_out_4 ), .out_2(\判断器2_1_out_2 ));
  \三路选择器  \u_三路选择器_1  (
    .in_1(\加法器_1_out_4 ), .in_2(\桶形移位器_1_out_4 ), .in_3(\逻辑运算_1_out_4 ), .in_4(\译码器_1_out_2 ), .out_5(C));
  \选择器  \u_选择器_3  (.in_1(\判断器_1_out_2 ), .in_2(\判断器2_1_out_2 ), .in_3(\译码器_1_out_2 ), .out_4(branch));
endmodule

module RF (
  input  in_1,
  input  in_2,
  input  in_3,
  input  in_4,
  input  in_5,
  output out_6,
  output out_7
);
endmodule

module SEXT (
  input  in_1,
  input  in_2,
  output out_3
);
endmodule

module SEXT2 (
  input  in_1,
  output out_2
);
endmodule

module \译码器  (
  input  in_1,
  output out_2
);
endmodule

module \桶形移位器  (
  input  in_1,
  input  in_2,
  input  in_3,
  output out_4
);
endmodule

module \逻辑运算  (
  input  in_1,
  input  in_2,
  input  in_3,
  output out_4
);
endmodule

module \加法器  (
  input  in_1,
  input  in_2,
  input  in_3,
  output out_4
);
endmodule

module \选择器  (
  input  in_1,
  input  in_2,
  input  in_3,
  output out_4
);
endmodule

module \三路选择器  (
  input  in_1,
  input  in_2,
  input  in_3,
  input  in_4,
  output out_5
);
endmodule

module \判断器  (
  input  in_1,
  output out_2
);
endmodule

module \判断器2  (
  input  in_1,
  output out_2
);
endmodule
